# Fritzing sketch Button_Selection_Basics (saved by Fritzing 0.9.3b)
circuit board: 8.46667cm x 5.64444cm
breadboards: 1

parts:
  S1 = Pushbutton [part_number=swgreen package="[THT]"]
  S2 = Pushbutton [part_number=swblue package="[THT]"]
  S3 = Pushbutton [part_number=swyellow package="[THT]"]
  S4 = Pushbutton [part_number=swred package="[THT]"]
  R1 = Resistor [tolerance=±5% resistance=10k package=THT]
  R2 = Resistor [tolerance=±5% resistance=10k package=THT]
  R3 = Resistor [tolerance=±5% resistance=10k package=THT]
  R4 = Resistor [tolerance=±5% resistance=10k package=THT]
  R5 = Resistor [tolerance=±5% resistance=220 part_number=rgreen package=THT]
  R6 = Resistor [tolerance=±5% resistance=220 part_number=rblue package=THT]
  R7 = Resistor [tolerance=±5% resistance=220 part_number=ryellow package=THT]
  R8 = Resistor [tolerance=±5% resistance=220 part_number=rred package=THT]
  LED1 = LED - 5mm [color="Green (570nm)" part_number=ledgreen package="5 mm [THT]"]
  LED2 = LED - 5mm [color="Red (633nm)" part_number=ledred package="5 mm [THT]"]
  LED3 = LED - 5mm [color="Yellow (595nm)" part_number=ledyellow package="5 mm [THT]"]
  Part1 = Arduino Nano (Rev3.0)
  LED4 = LED - 5mm [color="Blue (525nm)" part_number=ledblue package="5 mm [THT]"]

nets:
  N1: S1.Pin_1, S1.Pin_2, S2.Pin_1, S2.Pin_2, S3.Pin_1, S3.Pin_2, S4.Pin_1, S4.Pin_2, Part1.5V
  N2: S1.Pin_3, S1.Pin_4, R1.Pin_1, Part1.D12/MISO
  N3: S2.Pin_3, S2.Pin_4, R2.Pin_1, Part1.D11/MOSI
  N4: S3.Pin_3, S3.Pin_4, R3.Pin_1, Part1.D10
  N5: S4.Pin_3, S4.Pin_4, R4.Pin_1, Part1.D9
  N6: R1.Pin_0, R2.Pin_0, R3.Pin_0, R4.Pin_0, LED1.cathode, LED2.cathode, LED3.cathode, Part1.GND, LED4.cathode
  N7: R5.Pin_0, Part1.D2, Part1.D7
  N8: R5.Pin_1, LED1.anode
  N9: R6.Pin_0, Part1.D6
  N10: R6.Pin_1, LED4.anode
  N11: R7.Pin_0, Part1.D5
  N12: R7.Pin_1, LED3.anode
  N13: R8.Pin_0, Part1.D4
  N14: R8.Pin_1, LED2.anode
