# Fritzing sketch Simple (saved by Fritzing 0.9.3b)
breadboards: 1

parts:
  Part1 = Arduino Uno (Rev3)
  Skylab = Grove Buzz

nets:
  5V: Part1.5V, Skylab.VCC
  GND: Part1.GND, Skylab.GND

notes:
  Kitchen Sink Modified
